# Fritzing sketch Auxiliary Circuit Board (saved by Fritzing 0.9.3b)

parts:
  Part1 = Arduino Uno (Rev3)
  U1 = 74HC595 [package="DIP16 [THT]"]
  U2 = 74HC595 [package="DIP16 [THT]"]
  R2 = Resistor [tolerance=±5% resistance=100k package=THT]
  R3 = Resistor [tolerance=±5% resistance=100k package=THT]
  Part4 = Arduino Prototyping Shield
  J1 = female pin header, 8 pins [form="♀ (female)"]
  J2 = female pin header, 10 pins [form="♀ (female)"]
  J3 = female pin header, 6 pins [form="♀ (female)"]
  J4 = female pin header, 8 pins [form="♀ (female)"]
  FSRs = mystery part, 9 pins [chip_label=FSRs]
  Screen = mystery part, 11 pins [chip_label=Screen]
  R1 = Resistor [tolerance=±5% resistance=100k package=THT]
  U3 = mystery part, 15 pins [chip_label=LEDs]
  J6 = female pin header, 3 pins [form="♀ (female)"]
  J8 = female pin header, 3 pins [form="♀ (female)"]
  J9 = female pin header, 3 pins [form="♀ (female)"]
  J10 = female pin header, 3 pins [form="♀ (female)"]
  J11 = female pin header, 3 pins [form="♀ (female)"]
  J12 = female pin header, 3 pins [form="♀ (female)"]
  J13 = female pin header, 1 pin [form="♀ (female)"]
  J7 = female pin header, 12 pins [form="♀ (female)"]
  U4 = mystery part, 2 pins [chip_label=DC]  # not connected

nets:
  N1: Part1.A0, Part1.A1, R2.Pin_1, Part4.A0, Part4.A1, J3.pin1, J3.pin2, FSRs.pin4, FSRs.pin5, R1.Pin_1
  N2: Part1.A2, R3.Pin_1, Part4.A2, J3.pin3, FSRs.pin6
  N3: Part1.A3, Part4.A3, J3.pin4
  A4: Part1.A4/SDA, Part4.A4, J3.pin5, Screen.pin4
  A5: Part1.A5/SCL, Part4.A5, J3.pin6, Screen.pin3
  N4: Part1.D8, Part4.D8, J2.pin10, Screen.pin5
  N5: Part1.D9_PWM, Part4.D9, J2.pin9, Screen.pin2, Screen.pin6, J13.pin1
  N6: Part1.D10_PWM/SS, Part4.D10, J2.pin8, Screen.pin7
  N7: Part1.D11_PWM/MOSI, Part4.D11, J2.pin7, Screen.pin8
  N8: Part1.D12/MISO, Part4.D12, J2.pin6, Screen.pin9
  N9: Part1.D13/SCK, Part4.D13, J2.pin5, Screen.pin10
  GND: Part1.GND, U1.GND, U2.GND, Part4.GND, Part4.N$27, Part4.N$28, Part4.N$36, Part4.N$37, Part4.N$93, Part4.N$118, Part4.N$263, Part4.N$282, Part4.N$335, Part4.N$336, Part4.N$385, J2.pin4, J4.pin6, J4.pin7, FSRs.pin7, FSRs.pin8, FSRs.pin9, Screen.pin11, U3.pin13, U3.pin14, U3.pin15, J6.pin1, J6.pin2, J6.pin3, J11.pin1, J11.pin2, J11.pin3, J12.pin1, J12.pin2, J12.pin3
  AREF: Part1.AREF, Part4.AREF, J2.pin3
  N10: Part1.D0/RX, Part4.D0(RX), J1.pin8
  N11: Part1.D1/TX, Part4.D1(TX), J1.pin7
  N12: Part1.D2, U1.SH_CP, U2.SH_CP, Part4.D2, Part4.N$153, Part4.N$234, Part4.N$236, Part4.N$395, Part4.N$408, J1.pin6
  N13: Part1.D3_PWM, U1.ST_CP, U2.ST_CP, Part4.D3, Part4.N$232, Part4.N$235, Part4.N$304, Part4.N$400, Part4.N$410, J1.pin5
  N14: Part1.D4, U1.DS, Part4.D4, Part4.N$143, Part4.N$155, J1.pin4
  N15: Part1.D5_PWM, Part4.D5, J1.pin3
  N16: Part1.D6_PWM, Part4.D6, J1.pin2
  N17: Part1.D7, Part4.D7, J1.pin1
  IOREF: Part1.ioref, Part4.IOREF, J4.pin1, J4.pin2
  N18: Part1.RESET, Part4.RESET, J4.pin3
  3.3V: Part1.3V3, Part4.3.3V, J4.pin4
  +5V: Part1.5V, U1.MR, U1.VCC, U2.MR, U2.VCC, R2.Pin_0, R3.Pin_0, Part4.+5V, Part4.N$33, Part4.N$34, Part4.N$39, Part4.N$41, Part4.N$42, Part4.N$64, Part4.N$88, Part4.N$178, Part4.N$190, Part4.N$237, Part4.N$239, Part4.N$267, Part4.N$311, Part4.N$331, Part4.N$332, Part4.N$370, Part4.N$371, Part4.N$372, Part4.N$378, Part4.N$399, J4.pin5, FSRs.pin1, FSRs.pin2, FSRs.pin3, Screen.pin1, R1.Pin_0, J8.pin1, J8.pin2, J8.pin3, J9.pin1, J9.pin2, J9.pin3, J10.pin1, J10.pin2, J10.pin3
  VIN: Part1.VIN, Part4.+9V, J4.pin8
  N19: U1.Q1, Part4.N$46, Part4.N$58, Part4.N$76, U3.pin2, J7.pin11
  N20: U1.Q2, Part4.N$95, Part4.N$107, Part4.N$284, Part4.N$286, U3.pin3, J7.pin10
  N21: U1.Q3, Part4.N$94, Part4.N$106, Part4.N$285, Part4.N$289, U3.pin4, J7.pin9
  N22: U1.Q4, Part4.N$272, Part4.N$273, Part4.N$290, Part4.N$291, U3.pin5, J7.pin8
  N23: U1.Q5, Part4.N$259, Part4.N$292, Part4.N$314, Part4.N$360, U3.pin6, J7.pin7
  N24: U1.Q6, Part4.N$261, Part4.N$315, Part4.N$359, Part4.N$363, U3.pin7, J7.pin6
  N25: U1.Q7, Part4.N$262, Part4.N$281, Part4.N$361, Part4.N$362, U3.pin8, J7.pin5
  N26: U1.Q7', U2.DS, Part4.N$240, Part4.N$268, Part4.N$305, Part4.N$310
  N27: U1.OE, Part4.N$251
  LED_0: U1.Q0, Part4.N$47, Part4.N$59, Part4.N$135, Part4.N$156, U3.pin1, J7.pin12
  N28: U2.Q1, Part4.N$295, Part4.N$298, Part4.N$358, Part4.N$365, U3.pin10, J7.pin3
  N29: U2.Q2, Part4.N$296, Part4.N$297, Part4.N$357, Part4.N$367, U3.pin11, J7.pin2
  N30: U2.Q3, Part4.N$57, Part4.N$299, Part4.N$317, Part4.N$356, U3.pin12, J7.pin1
  N31: U2.Q4, Part4.N$319
  N32: U2.Q5, Part4.N$17
  N33: U2.Q6, Part4.N$52
  N34: U2.Q7, Part4.N$383
  N35: U2.Q7', Part4.N$396
  N36: U2.OE, Part4.N$16
  LED_8: U2.Q0, Part4.N$45, Part4.N$269, Part4.N$307, Part4.N$364, U3.pin9, J7.pin4
  N37: Part4.SDA, J2.pin2
  N38: Part4.SCL, J2.pin1

notes:
  1. Holes in the enclosure should be cut only horizontally, right over the headers.
  2. The following are on bottom side of shield:
  2.1 Grey 'jumpers' i.e. solder joints
  2.2 Diagonal power (red and black) jumpers
  2.3 Resistors
  3. Black boxes outside are peripherals from whom incoming wires will connect to headers.
  4. May need IC sockets instead of soldering shift registers straight to board?
  5. Make sure to leave hole in enclosure (on the side, if not already left open) for wall adapter wire also.
